# Fritzing sketch wiring (saved by Fritzing 0.9.3b)
perfboards: 1

parts:
  JACK1 = 2.1mm DC Barrel Jack [part_number=12V]
  Part2 = Arduino Nano (Rev3.0) (ICSP)
  J18 = Generic male header - 3 pins [form="♀ (female)" package=THT]
  R1 = Resistor [tolerance=±5% resistance=220 package=THT]
  J21 = Generic male header - 3 pins [form="♀ (female)" package=THT]
  J22 = Generic male header - 3 pins [form="♀ (female)" package=THT]
  J23 = Generic male header - 3 pins [form="♀ (female)" package=THT]
  J24 = Generic male header - 3 pins [form="♀ (female)" package=THT]
  J27 = Generic male header - 3 pins [form="♀ (female)" package=THT]
  J28 = Generic male header - 3 pins [form="♀ (female)" package=THT]
  J29 = Generic male header - 3 pins [form="♀ (female)" package=THT]
  J30 = Generic male header - 3 pins [form="♀ (female)" package=THT]
  J31 = Generic male header - 3 pins [form="♀ (female)" package=THT]
  C3 = Electrolytic Capacitor [capacitance=47µF voltage=50V package="100 mil [THT, electrolytic]"]
  C4 = Electrolytic Capacitor [capacitance=0.47mF voltage=50V package="100 mil [THT, electrolytic]"]
  Q1 = MOSFET-NCHANNEL [part_number=AO3400 package=to220v]
  D1 = Rectifier Diode [part_number="1N4001 or M1" breakdown_voltage=3.6V package="300 mil [THT]"]

nets:
  N1: JACK1.center, Part2.VIN, J27.Pin_2, C4.+
  N2: JACK1.sleeve, Part2.GND, J28.Pin_2, C4.-, Q1.S
  N3: Part2.D2, Q1.G
  N4: Part2.D3, J28.Pin_3
  N5: Part2.D6, J23.pin_1
  N6: Part2.D7, J21.Pin_1
  N7: Part2.D8, J21.Pin_2
  N8: Part2.D9, J21.Pin_3
  N9: Part2.D10, J22.Pin_1
  N10: Part2.D11/MOSI, J22.Pin_2
  N11: Part2.D12/MISO, J22.Pin_3
  N12: Part2.5V, J18.Pin_3, C3.+
  N13: Part2.A7, R1.Pin_0, J28.Pin_1
  N14: Part2.A5, J30.pin_1
  N15: Part2.A4, J31.pin_1
  N16: Part2.A3, J29.pin_1
  N17: Part2.D13/SCK, J24.pin_1
  N18: J18.Pin_2, C3.-
  N19: J27.Pin_3, Q1.D, D1.anode

custom parts:
  2.1mm DC Barrel Jack: 2.1mm DC Barrel Jack with Thru-Hole Connectors (breadboardable)
  Generic male header - 3 pins: Generic male header
  Generic male header - 3 pins: Generic male header
